# Fritzing sketch board (saved by Fritzing 0.9.5d)
perfboards: 1

parts:
  Part2 = Arduino Nano (Rev3.0)  # not connected
  X1 = USB Connectors [package=usb-a-pcb]  # not connected
  S1 = Pushbutton [package="[THT]"]
  S2 = Pushbutton [package="[THT]"]
  J1 = JST-VHR-3N [part_number=JST-VHR-3N package=THT]  # not connected
  R1 = Resistor [tolerance=±5% resistance=220 package="0402 [SMD]"]
  R2 = Resistor [tolerance=±5% resistance=220 package="0402 [SMD]"]  # not connected

nets:
  N1: S1.Pin_1, S1.Pin_2, R1.Pin_0
  N2: S1.Pin_3, S1.Pin_4
  N3: S2.Pin_1, S2.Pin_2
  N4: S2.Pin_3, S2.Pin_4

notes:
  Only pins 2 and 3 support interrupts on the 328p-based nano
  pretend this is USB-C
  PWM: (3), 5, 6, 9, 10, 11
  3-pin JST with clip
